# Fritzing sketch ESP8266-Blink (saved by Fritzing 0.8.3b)
breadboards: 1

parts:
  R1 = Resistor [tolerance=±5% resistance=10k package=THT]
  R2 = Resistor [tolerance=±5% resistance=10k package=THT]  # not connected
  R3 = Resistor [tolerance=±5% resistance=10k package=THT]
  R4 = Resistor [tolerance=±5% resistance=10k package=THT]
  R5 = Resistor [tolerance=±5% resistance=10k package=THT]
  S1 = Pushbutton [package="[THT]"]
  S2 = Pushbutton [package="[THT]"]
  LED1 = LED - 5mm [color="Red (633nm)" package="5 mm [THT]"]  # not connected
  R6 = Resistor [tolerance=±5% resistance=1k package=THT]  # not connected

nets:
  N1: R1.Pin_0, R3.Pin_0, R4.Pin_0, R5.Pin_0
  N2: R4.Pin_1, S2.Pin_3, S2.Pin_4
  N3: R5.Pin_1, S1.Pin_3, S1.Pin_4
  N4: S1.Pin_1, S1.Pin_2, S2.Pin_1, S2.Pin_2
