# Fritzing sketch ButtonAndBuzzer (saved by Fritzing 0.8.3b)
breadboards: 1

parts:
  パーツ1 = Arduino Uno (Rev3)
  J1 = Piezo Speaker
  S1 = Momentary Switch [package=ksa_sealed_tac_switch]
  R1 = Resistor [tolerance=±5% resistance=10k package=THT]

nets:
  N1: パーツ1.GND, J1.pin1, R1.Pin_0
  N2: パーツ1.D9_PWM, J1.pin2
  N3: パーツ1.D2, S1.4, R1.Pin_1
  N4: パーツ1.5V, S1.2
